# Fritzing sketch devre şema (saved by Fritzing 1.0.6)
perfboards: 1

parts:
  M1 = DOIT Esp32 DevKit v1 (30 pins long, 11 pins width) [part_number=ESP32S-PIN30]
  C1 = Capacitor Polarized [package=panasonic_h13]
  Driver1 = 28BYJ-48 Driver Module [part_number=ULN2003 package=THT]
  LED1 = LED - 5mm [color="Yellow (585nm)" current=0.030A package="5 mm [THT]"]
  LED2 = LED - 5mm [color="Yellow (585nm)" current=0.030A package="5 mm [THT]"]
  R1 = Resistor [tolerance=±5% power=0.25W resistance=220 package=THT]
  R2 = Resistor [tolerance=±5% power=0.25W resistance=220 package=THT]
  S1 = Momentary Switch 6mm 2pin
  JACK1 = 2.1mm DC Barrel Jack
  S2 = Round Pushbutton

nets:
  N1: M1.GND, C1.-, JACK1.sleeve
  N2: M1.D4, R2.Pin_0
  N3: M1.D5, R1.Pin_0
  N4: M1.D18, Driver1.IN1
  N5: M1.D19, Driver1.IN2
  N6: M1.D21, Driver1.IN3
  N7: M1.D22, Driver1.IN4
  N8: M1.VIN, C1.+, S2.leg1
  N9: LED1.cathode, LED2.cathode, S1.2
  N10: LED1.anode, R2.Pin_1
  N11: LED2.anode, R1.Pin_1
  N12: JACK1.center, S2.leg0

custom parts:
  DOIT Esp32 DevKit v1 (30 pins long, 11 pins width): The DOIT Esp32 DevKit v1 is one of the development board created by DOIT to evaluate the ESP-WROOM-32 module. It is based on the ESP32 microcontroller that boasts Wifi, Bluetooth, Ethernet and Low Power support all in a single chip. (vanepp) made breadboard work, adjusted pin numbering and labels and reduced size of schematic and cleaned up pcb. This chip is 30pins long (2 x15) and 11 pins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
  28BYJ-48 Driver Module: Generic male header
  Momentary Switch 6mm 2pin: Momentary Switch 6mm 2 pin Button commonly used for reset or general input.
  2.1mm DC Barrel Jack: 2.1mm DC Barrel Jack with Thru-Hole Connectors (breadboardable)
